// Logisim project inmultire.circ as structural Verilog: 4 circuits, main circuit model de inbus
module model_de_inbus (
  input  semnal_de_control,
  input  alt_semnal_de_control,
  input  [7:0] inbus,
  output [7:0] out_4,
  output [7:0] out_5
);

  wire clock_1_out;
  wire [7:0] controlled_buffer_1_out, controlled_buffer_2_out;

  Clock clock_1 (.out(clock_1_out));
  Register register_1 (.D(controlled_buffer_1_out), .en(semnal_de_control), .Q(out_4), .clk(clock_1_out));  // open: clr
  assign controlled_buffer_1_out = semnal_de_control ? inbus : 8'bz;  // Controlled_Buffer controlled_buffer_1
  Register register_2 (
    .D(controlled_buffer_2_out), .en(alt_semnal_de_control), .Q(out_5), .clk(clock_1_out));  // open: clr
  assign controlled_buffer_2_out = alt_semnal_de_control ? inbus : 8'bz;  // Controlled_Buffer controlled_buffer_2
endmodule

module counter (
  input  in_1,
  input  in_2,
  input  in_3,
  output [1:0] out_4
);

  wire not_1_out;

  J_K_Flip_Flop j_k_ff_1 (.J(in_2), .clk(in_1), .K(in_2), .Q(out_4[0]), .reset(not_1_out));  // open: Qn, preset, en
  not not_1 (not_1_out, in_3);
  J_K_Flip_Flop #(.trigger("falling")) j_k_ff_2 (
    .J(in_2), .clk(out_4[0]), .K(in_2), .Q(out_4[1]), .reset(not_1_out));  // open: Qn, preset, en
endmodule

module Sequence_CNT (
  input  in_1,
  input  in_2,
  input  in_3,
  input  in_4,
  output out_5,
  output out_6,
  output out_7,
  output out_8
);

  wire and_1_out, and_2_out, s_r_ff_1_q;
  wire [1:0] counter_1_out_4;

  S_R_Flip_Flop s_r_ff_1 (.S(in_1), .clk(in_3), .R(in_2), .Q(s_r_ff_1_q));  // open: Qn, preset, reset, en
  counter counter_1 (.out_4(counter_1_out_4), .in_3(and_2_out), .in_1(and_1_out), .in_2(in_3));
  and and_1 (and_1_out, s_r_ff_1_q, in_3);
  and and_2 (and_2_out, in_4, s_r_ff_1_q);
  Decoder #(.select(2), .enable("false")) decoder_1 (
    .out0(out_5), .out1(out_6), .out2(out_7), .out3(out_8), .sel(counter_1_out_4));
endmodule

module Control_Unit_inmultire (
  input  Begin,
  input  CLK,
  input  nRST,
  input  Q_0,
  input  Q__1,
  input  Count7,
  output c0,
  output c1,
  output c2,
  output c3,
  output c4,
  output c5,
  output c6
);

  wire and_1_out, and_2_out, Cycle_0_q, Cycle_1_8_q, Cycle_9_q, not_1_out, not_2_out, not_3_out, not_4_out,
       not_5_out, not_6_out, not_7_out, not_8_out, not_9_out, not_10_out, not_11_out, not_12_out,
       sequence_cnt_1_out_5, sequence_cnt_1_out_6, sequence_cnt_1_out_7, xor_1_out;

  S_R_Flip_Flop Cycle_0 (.S(Begin), .clk(CLK), .R(and_1_out), .Q(Cycle_0_q));  // open: Qn, preset, reset, en
  S_R_Flip_Flop Cycle_1_8 (.S(and_1_out), .clk(CLK), .R(and_2_out), .Q(Cycle_1_8_q));  // open: Qn, preset, reset, en
  S_R_Flip_Flop Cycle_9 (.S(and_2_out), .clk(CLK), .R(not_2_out), .Q(Cycle_9_q));  // open: Qn, preset, reset, en
  and and_1 (and_1_out, Cycle_0_q, sequence_cnt_1_out_7);
  and and_2 (and_2_out, Cycle_1_8_q, Count7, sequence_cnt_1_out_7);
  not not_1 (not_1_out, not_5_out);
  not not_2 (not_2_out, not_1_out);
  not not_3 (not_3_out, not_8_out);
  not not_4 (not_4_out, not_3_out);
  not not_5 (not_5_out, not_4_out);
  not not_6 (not_6_out, not_7_out);
  not not_7 (not_7_out, not_10_out);
  not not_8 (not_8_out, not_6_out);
  Sequence_CNT sequence_cnt_1 (
    .in_1(Begin), .in_2(not_2_out), .in_3(CLK), .in_4(nRST), .out_5(sequence_cnt_1_out_5),
    .out_6(sequence_cnt_1_out_6), .out_7(sequence_cnt_1_out_7));  // open: out_8
  not not_9 (not_9_out, not_11_out);
  not not_10 (not_10_out, not_9_out);
  not not_11 (not_11_out, not_12_out);
  not not_12 (not_12_out, c6);
  xor xor_1 (xor_1_out, Q_0, Q__1);
  and and_3 (c0, sequence_cnt_1_out_5, Cycle_0_q);
  and and_4 (c1, sequence_cnt_1_out_6, Cycle_0_q);
  and and_5 (c2, Cycle_1_8_q, sequence_cnt_1_out_5, xor_1_out);
  and and_6 (c3, c2, Q_0, ~Q__1);  // AND_Gate
  and and_7 (c4, sequence_cnt_1_out_6, Cycle_1_8_q, ~Count7);  // AND_Gate
  and and_8 (c5, sequence_cnt_1_out_5, Cycle_9_q);
  and and_9 (c6, sequence_cnt_1_out_6, Cycle_9_q);
endmodule
